# Fritzing sketch CarAcc2 (saved by Fritzing 0.9.4)
circuit board: 5.66155cm x 4.43858cm
breadboards: 1

parts:
  IC1 = PICAXE-08 [part_number=PIC12F package=THT]
  Q1 = TRANSISTOR_NPN [package=to-92-ammo]
  R1 = Resistor [tolerance=±5% resistance=10k package=THT]
  R2 = Resistor [tolerance=±5% resistance=10k package=THT]
  U1 = Voltage Regulator - 5V [package="TO220 [THT]"]
  C1 = Electrolytic Capacitor [capacitance=100µF package="100 mil [THT, electrolytic]"]
  C2 = Electrolytic Capacitor [capacitance=10µF package="100 mil [THT, electrolytic]"]
  C3 = Ceramic Capacitor [capacitance=100nF package="100 mil [THT, multilayer]"]
  Q4 = NPN-Transistor [package="TO92 [THT]"]
  R3 = Resistor [tolerance=±5% resistance=10k package=THT]
  R4 = Resistor [tolerance=±5% resistance=1k package=THT]
  Q3 = Basic FET P-Channel [part_number=2SJ334 package="TO220 [THT]"]
  R5 = Resistor [tolerance=±5% resistance=1k package=THT]
  J1 = Screw terminal - 2 pins [package=THT]
  R6 = Resistor [tolerance=±5% resistance=10k package=THT]
  R7 = Resistor [tolerance=±5% resistance=4.7k package=THT]
  R8 = Resistor [tolerance=±5% resistance=10k package=THT]
  Q5 = NPN-Transistor [package="TO92 [THT]"]
  R9 = Resistor [tolerance=±5% resistance=10k package=THT]
  R10 = Resistor [tolerance=±5% resistance=4.7k package=THT]
  J2 = Screw terminal - 2 pins [package=THT]
  J3 = Screw terminal - 2 pins [package=THT]

nets:
  N1: IC1.+V, R1.Pin_1, U1.output_voltage, C2.+, C3.1, R8.Pin_1
  N2: IC1.Serial_In, Q1.C, R1.Pin_0
  N3: IC1.In/Out_4, R8.Pin_0, Q5.C
  N4: IC1.Serial_Out_/_Out_0, R3.Pin_0
  Body/GND: IC1.0V, Q1.E, U1.GND, C1.-, C2.-, C3.0, Q4.E, J1.pin1, R6.Pin_0, R7.Pin_0, Q5.E, R10.Pin_0, J3.pin2
  N5: Q1.B, R2.Pin_1, R7.Pin_1
  ACC: R2.Pin_0, J2.pin2
  Battery: U1.input_voltage, C1.+, Q3.source, R5.Pin_1, J2.pin1
  N6: Q4.B, R3.Pin_1, R6.Pin_1
  N7: Q4.C, R4.Pin_0
  N8: R4.Pin_1, Q3.gate, R5.Pin_0
  N9: Q3.drain, J1.pin2
  N10: Q5.B, R9.Pin_1, R10.Pin_1
  Reset: R9.Pin_0, J3.pin1

notes:
  +12v
  +5v
